# Fritzing sketch UltrasonicSensor_Arduino (saved by Fritzing 0.9.3b)
breadboards: 2

parts:
  Part1 = Arduino Nano (Rev3.0)
  hc-sr1 = hc-sr04
  U1 = LCD-16X2 [package=lcd-16x2_noholes]

nets:
  GND: Part1.GND, hc-sr1.GND, U1.VSS, U1.R_W, U1.K
  N1: Part1.D2, U1.DB7
  N2: Part1.D3, U1.DB6
  N3: Part1.D4, U1.DB5
  N4: Part1.D5, U1.DB4
  N5: Part1.D6, U1.VO
  N6: Part1.D9, hc-sr1.Echo
  N7: Part1.D10, hc-sr1.Trig
  N8: Part1.D11/MOSI, U1.E
  N9: Part1.D12/MISO, U1.RS
  5V: Part1.5V, hc-sr1.VCC, U1.VDD, U1.A

// code stored in the sketch: Ultrasonic.ino
#include <NewPing.h>
#include <LiquidCrystal.h> 
int Contrast=110;
LiquidCrystal lcd(12, 11, 5, 4, 3, 2);  

NewPing sonar(9, 10, 500); // NewPing setup of pins and maximum distance.
float distance;

void setup()
{
     analogWrite(6,Contrast);
     lcd.begin(16, 2);
     Serial.begin(9600);
     lcd.setCursor(0, 0);
     lcd.print("*Evoneg Tech*");
} 
void loop()
{ 
    delay(250); // Wait 250ms between measures. 
  
    distance = sonar.ping_cm();

    lcd.setCursor(0, 1);
    if (distance >0)
    {
       lcd.print("Distance = ");
       lcd.print(distance,0);
       lcd.print("cm  ");  
    }   
    else
    {
         lcd.print("....Measuring...");
    }
}
